# Fritzing sketch sens_umid_DIY (saved by Fritzing 0.9.3b)
breadboards: 1

parts:
  Part2 = Arduino Uno (Rev3) - ICSP
  Part3 = Soil Moisture Sensor
  R1 = Resistor [tolerance=±5% resistance=10k package=THT]
  DS1 = DS18B20 1-Wire Temperature Sensor [part_number=DS18B20]
  R2 = Resistor [tolerance=±5% resistance=4.7k package="2010 [SMD]"]
  RHT1 = Humidity and Temperature Sensor RHT03
  R3 = Resistor [tolerance=±5% resistance=10k package=THT]

nets:
  N1: Part2.A0, Part3.SIG, R1.Pin_0
  N2: Part2.A1, RHT1.Data-signal, R3.Pin_0
  N3: Part2.D2, DS1.DQ, R2.Pin_1
  5V: Part2.5V, R1.Pin_1, DS1.VDD, R2.Pin_0, RHT1.Vcc, R3.Pin_1
  GND: Part2.GND, Part3.GND, DS1.GND, RHT1.GND_2
